# Fritzing sketch meter (saved by Fritzing 1.0.7)
circuit board: 8.46667cm x 5.64444cm

parts:
  Proto = Adafruit FeatherWing Doubler [part_number="Adafruit #2890"]
  JBUS = screw terminal, 3 pins
  JMETER = screw terminal, 3 pins
  R1 = Resistor Mini [tolerance=±5% resistance=10k package=THT]
  R2 = Resistor Mini [tolerance=±5% resistance=10k package=THT]
  R3 = Resistor Mini [tolerance=±5% resistance=1k package=THT]
  R4 = Resistor Mini [tolerance=±5% resistance=10k package=THT]
  D2 = Small signal Diode flat 300mil [part_number=1N4148 package="300 mil [THT]"]
  D1 = Small signal Diode flat 300mil [part_number=1N4148 package="300 mil [THT]"]
  C1 = Ceramic Capacitor [capacitance=100nF voltage=35V package="100 mil [THT, multilayer]"]
  U1 = Voltage Regulator - 5V [part_number=L7805CV package="TO220 [THT]"]
  C2 = Ceramic Capacitor [capacitance=100nF voltage=35V package="100 mil [THT, multilayer]"]
  C3 = Ceramic Capacitor [capacitance=100nF voltage=35V package="100 mil [THT, multilayer]"]
  Arduino = Arduino Uno (Rev3)
  C4 = Ceramic Capacitor [capacitance=1µF voltage=35V package="100 mil [THT, multilayer]"]

nets:
  JBUS_In: Proto.EN, Proto.N, JBUS.pin1, R3.Pin_1, U1.input_voltage, C2.1
  Arduino_A1: Proto.O, Proto.3V, Proto.N$137, R1.Pin_0, R2.Pin_0, R4.Pin_0, D2.anode, D1.cathode, C1.0, Arduino.A1
  GND: Proto.M, Proto.GND, Proto.N$37, JBUS.pin3, JMETER.pin1, R1.Pin_1, R2.Pin_1, D1.anode, C1.1, U1.GND, C2.0, C3.0, Arduino.GND, C4.0
  Arduino_5V: Proto.L, Proto.N$126, D2.cathode, U1.output_voltage, C3.1, Arduino.ioref
  Arduino_D5: Proto.B, Proto.N$212, JMETER.pin3, Arduino.D5_PWM, C4.1
  N1: Proto.N$59, R3.Pin_0, R4.Pin_1

custom parts:
  Adafruit FeatherWing Doubler: This is the FeatherWing Doubler - a prototyping add-on and more for all Feather boards. This is similar to our FeatherWing Proto except there are two! The magic of the Doubler comes when stacking a Feather and another board on top of the Doubler so you can work with both boards simultaneously side-by-side! The Doubler, like the Proto, has a duplicate breakout for each pin on a Feather, as well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
  Resistor Mini: A generic resistor (0.25W)
  Small signal Diode flat 300mil: Small signal diode such as the 1n4148 Footprint: mounted flat on 300mil centers.
